// Logisim project UAL.circ as structural Verilog: 11 circuits, main circuit OR 4BIT
module OR_4BIT (
  input  [3:0] A,
  input  [3:0] B,
  output [3:0] OR
);

  or or_1 (OR[0], A[0], B[0]);
  or or_2 (OR[1], A[1], B[1]);
  or or_3 (OR[2], A[2], B[2]);
  or or_4 (OR[3], A[3], B[3]);
endmodule

module AND_4BIT (
  input  [3:0] A,
  input  [3:0] B,
  output [3:0] AND
);

  and and_1 (AND[0], A[0], B[0]);
  and and_2 (AND[1], A[1], B[1]);
  and and_3 (AND[2], A[2], B[2]);
  and and_4 (AND[3], A[3], B[3]);
endmodule

module XOR_4BIT (
  input  [3:0] A,
  input  [3:0] B,
  output [3:0] XOR
);

  xor xor_1 (XOR[0], A[0], B[0]);
  xor xor_2 (XOR[1], A[1], B[1]);
  xor xor_3 (XOR[2], A[2], B[2]);
  xor xor_4 (XOR[3], A[3], B[3]);
endmodule

module nonA (
  input  [3:0] A,
  output [3:0] minus_A
);

  not not_1 (minus_A[0], A[0]);
  not not_2 (minus_A[1], A[1]);
  not not_3 (minus_A[2], A[2]);
  not not_4 (minus_A[3], A[3]);
endmodule

module ADD1BIT (
  input  A,
  input  B,
  input  RIN,
  output S,
  output ROUT
);

  wire and_1_out, and_2_out, and_3_out, and_4_out, and_5_out, and_6_out, and_7_out, not_1_out, not_2_out,
       not_3_out, not_4_out, not_5_out, not_6_out;

  not not_1 (not_1_out, A);
  not not_2 (not_2_out, B);
  not not_3 (not_3_out, A);
  not not_4 (not_4_out, RIN);
  not not_5 (not_5_out, B);
  not not_6 (not_6_out, RIN);
  and and_1 (and_1_out, B, RIN);
  and and_2 (and_2_out, A, RIN);
  and and_3 (and_3_out, A, B);
  and and_4 (and_4_out, not_1_out, not_2_out, RIN);
  and and_5 (and_5_out, not_3_out, B, not_4_out);
  and and_6 (and_6_out, A, not_5_out, not_6_out);
  and and_7 (and_7_out, A, B, RIN);
  or or_1 (ROUT, and_1_out, and_2_out, and_3_out);
  or or_2 (S, and_4_out, and_5_out, and_6_out, and_7_out);
endmodule

module ADD_4BIT (
  input  [3:0] A,
  input  [3:0] B,
  input  RIN,
  output ROUT,
  output S3,
  output S2,
  output S1,
  output S0
);

  wire add1bit_2_rout, add1bit_3_rout, add1bit_4_rout;

  ADD1BIT add1bit_1 (.A(A[3]), .B(B[3]), .RIN(add1bit_2_rout), .S(S3), .ROUT(ROUT));
  ADD1BIT add1bit_2 (.A(A[2]), .B(B[2]), .RIN(add1bit_3_rout), .S(S2), .ROUT(add1bit_2_rout));
  ADD1BIT add1bit_3 (.A(A[1]), .B(B[1]), .RIN(add1bit_4_rout), .S(S1), .ROUT(add1bit_3_rout));
  ADD1BIT add1bit_4 (.A(A[0]), .B(B[0]), .RIN(RIN), .S(S0), .ROUT(add1bit_4_rout));
endmodule

module B_BAR (
  input  [3:0] b,
  input  B_BAR,
  output B3,
  output B2,
  output B1,
  output B0
);

  xor xor_1 (B3, B_BAR, b[3]);
  xor xor_2 (B2, B_BAR, b[2]);
  xor xor_3 (B1, B_BAR, b[1]);
  xor xor_4 (B0, B_BAR, b[0]);
endmodule

module ADD_SUB (
  input  [3:0] A,
  input  plus_OU_minus,
  input  [3:0] B,
  output [3:0] s,
  output signe
);

  wire add_4bit_1_rout, add_4bit_2_rout;
  wire [3:0] add_4bit_1_s0, b_bar_1_b0, b_bar_2_b0;

  ADD_4BIT add_4bit_1 (
    .ROUT(add_4bit_1_rout), .S3(add_4bit_1_s0[3]), .S2(add_4bit_1_s0[2]), .S1(add_4bit_1_s0[1]),
    .S0(add_4bit_1_s0[0]), .A(A), .B(b_bar_2_b0), .RIN(plus_OU_minus));
  B_BAR b_bar_1 (
    .B3(b_bar_1_b0[3]), .B2(b_bar_1_b0[2]), .B1(b_bar_1_b0[1]), .B0(b_bar_1_b0[0]), .b(add_4bit_1_s0),
    .B_BAR(signe));
  ADD_4BIT add_4bit_2 (
    .ROUT(add_4bit_2_rout), .S3(s[3]), .S2(s[2]), .S1(s[1]), .S0(s[0]), .A(4'b0000), .B(b_bar_1_b0),
    .RIN(signe));
  B_BAR b_bar_2 (
    .B3(b_bar_2_b0[3]), .B2(b_bar_2_b0[2]), .B1(b_bar_2_b0[1]), .B0(b_bar_2_b0[0]), .b(B),
    .B_BAR(plus_OU_minus));
  and and_1 (signe, add_4bit_1_s0[3], plus_OU_minus);
  // also tied to GND on the sheet: {add_4bit_1_rout, add_4bit_2_rout}
endmodule

module MUX (
  input  [3:0] in_1,
  input  [3:0] in_2,
  input  [3:0] in_3,
  input  [3:0] in_4,
  input  [3:0] in_5,
  input  in_6,
  input  in_7,
  input  in_8,
  output [3:0] out_9
);

  wire not_1_out, not_2_out, not_3_out, not_4_out, not_5_out, not_6_out;
  wire [3:0] and_1_out, and_5_out, and_9_out, and_13_out, and_17_out, and_21_out, and_25_out, and_29_out,
       and_33_out, or_1_out, or_2_out, or_3_out;

  not not_1 (not_1_out, not_2_out);
  not not_2 (not_2_out, not_3_out);
  not not_3 (not_3_out, not_4_out);
  not not_4 (not_4_out, in_6);
  and and_1 (and_1_out[0], in_1[0], not_1_out);
  and and_2 (and_1_out[1], in_1[1], not_1_out);
  and and_3 (and_1_out[2], in_1[2], not_1_out);
  and and_4 (and_1_out[3], in_1[3], not_1_out);
  and and_5 (and_5_out[0], in_2[0], not_2_out);
  and and_6 (and_5_out[1], in_2[1], not_2_out);
  and and_7 (and_5_out[2], in_2[2], not_2_out);
  and and_8 (and_5_out[3], in_2[3], not_2_out);
  and and_9 (and_9_out[0], in_3[0], not_3_out);
  and and_10 (and_9_out[1], in_3[1], not_3_out);
  and and_11 (and_9_out[2], in_3[2], not_3_out);
  and and_12 (and_9_out[3], in_3[3], not_3_out);
  and and_13 (and_13_out[0], in_4[0], not_4_out);
  and and_14 (and_13_out[1], in_4[1], not_4_out);
  and and_15 (and_13_out[2], in_4[2], not_4_out);
  and and_16 (and_13_out[3], in_4[3], not_4_out);
  and and_17 (and_17_out[0], in_5[0], in_6);
  and and_18 (and_17_out[1], in_5[1], in_6);
  and and_19 (and_17_out[2], in_5[2], in_6);
  and and_20 (and_17_out[3], in_5[3], in_6);
  assign or_1_out = and_1_out | and_5_out;  // OR_Gate or_1, 4 bits wide
  assign or_2_out = and_9_out | and_13_out;  // OR_Gate or_2, 4 bits wide
  not not_5 (not_5_out, in_7);
  and and_21 (and_21_out[0], or_1_out[0], not_5_out);
  and and_22 (and_21_out[1], or_1_out[1], not_5_out);
  and and_23 (and_21_out[2], or_1_out[2], not_5_out);
  and and_24 (and_21_out[3], or_1_out[3], not_5_out);
  and and_25 (and_25_out[0], or_2_out[0], in_7);
  and and_26 (and_25_out[1], or_2_out[1], in_7);
  and and_27 (and_25_out[2], or_2_out[2], in_7);
  and and_28 (and_25_out[3], or_2_out[3], in_7);
  assign or_3_out = and_21_out | and_25_out;  // OR_Gate or_3, 4 bits wide
  and and_29 (and_29_out[0], or_3_out[0], not_6_out);
  and and_30 (and_29_out[1], or_3_out[1], not_6_out);
  and and_31 (and_29_out[2], or_3_out[2], not_6_out);
  and and_32 (and_29_out[3], or_3_out[3], not_6_out);
  not not_6 (not_6_out, in_8);
  and and_33 (and_33_out[0], and_17_out[0], in_8);
  and and_34 (and_33_out[1], and_17_out[1], in_8);
  and and_35 (and_33_out[2], and_17_out[2], in_8);
  and and_36 (and_33_out[3], and_17_out[3], in_8);
  assign out_9 = and_29_out | and_33_out;  // OR_Gate or_4, 4 bits wide
endmodule

module decodeur (
  input  OR,
  input  AND,
  input  XOR,
  input  Abar,
  input  ADD,
  input  SUB,
  output a,
  output b,
  output c,
  output d
);

  wire and_1_out, and_2_out, and_3_out, and_4_out, and_5_out, and_6_out, and_7_out, and_8_out, not_1_out,
       not_2_out, not_3_out, not_4_out, not_5_out, not_6_out, not_7_out, not_8_out, not_9_out, not_10_out,
       not_11_out, not_12_out, not_13_out, not_14_out, not_15_out, not_16_out, not_17_out, not_18_out,
       not_19_out, not_20_out, not_21_out, not_22_out, not_23_out, not_24_out, not_25_out, not_26_out,
       not_27_out, not_28_out, not_29_out, not_30_out, not_31_out, not_32_out, not_33_out, not_34_out,
       not_35_out, not_36_out, not_37_out, not_38_out, not_39_out, not_40_out, not_41_out, not_42_out,
       not_43_out, not_44_out, not_45_out;

  not not_1 (not_1_out, OR);
  not not_2 (not_2_out, AND);
  not not_3 (not_3_out, XOR);
  not not_4 (not_4_out, Abar);
  not not_5 (not_5_out, ADD);
  not not_6 (not_6_out, OR);
  not not_7 (not_7_out, AND);
  not not_8 (not_8_out, XOR);
  not not_9 (not_9_out, Abar);
  not not_10 (not_10_out, SUB);
  not not_11 (not_11_out, OR);
  not not_12 (not_12_out, AND);
  not not_13 (not_13_out, Abar);
  not not_14 (not_14_out, ADD);
  not not_15 (not_15_out, SUB);
  not not_16 (not_16_out, AND);
  not not_17 (not_17_out, XOR);
  not not_18 (not_18_out, Abar);
  not not_19 (not_19_out, ADD);
  not not_20 (not_20_out, SUB);
  not not_21 (not_21_out, OR);
  not not_22 (not_22_out, AND);
  not not_23 (not_23_out, XOR);
  not not_24 (not_24_out, ADD);
  not not_25 (not_25_out, SUB);
  not not_26 (not_26_out, OR);
  not not_27 (not_27_out, AND);
  not not_28 (not_28_out, Abar);
  not not_29 (not_29_out, ADD);
  not not_30 (not_30_out, SUB);
  not not_31 (not_31_out, OR);
  not not_32 (not_32_out, AND);
  not not_33 (not_33_out, XOR);
  not not_34 (not_34_out, Abar);
  not not_35 (not_35_out, ADD);
  not not_36 (not_36_out, OR);
  not not_37 (not_37_out, AND);
  not not_38 (not_38_out, XOR);
  not not_39 (not_39_out, Abar);
  not not_40 (not_40_out, SUB);
  not not_41 (not_41_out, OR);
  not not_42 (not_42_out, AND);
  not not_43 (not_43_out, XOR);
  not not_44 (not_44_out, Abar);
  not not_45 (not_45_out, ADD);
  and and_1 (and_1_out, not_1_out, not_2_out, not_3_out, not_4_out, not_5_out, SUB);
  and and_2 (and_2_out, not_6_out, not_7_out, not_8_out, not_9_out, ADD, not_10_out);
  and and_3 (and_3_out, not_11_out, not_12_out, XOR, not_13_out, not_14_out, not_15_out);
  and and_4 (and_4_out, OR, not_16_out, not_17_out, not_18_out, not_19_out, not_20_out);
  and and_5 (and_5_out, not_21_out, not_22_out, not_23_out, Abar, not_24_out, not_25_out);
  and and_6 (and_6_out, not_26_out, not_27_out, XOR, not_28_out, not_29_out, not_30_out);
  and and_7 (and_7_out, not_31_out, not_32_out, not_33_out, not_34_out, not_35_out, SUB);
  and and_8 (and_8_out, not_36_out, not_37_out, not_38_out, not_39_out, ADD, not_40_out);
  and and_9 (d, not_41_out, not_42_out, not_43_out, not_44_out, not_45_out, SUB);
  or or_1 (a, and_1_out, and_2_out, and_3_out, and_4_out);
  or or_2 (b, and_5_out, and_6_out);
  or or_3 (c, and_7_out, and_8_out);
endmodule

module CPU (
  input  [3:0] A,
  input  [3:0] B,
  input  SUB,
  input  ADD,
  input  XOR,
  input  AND,
  input  OR,
  input  Abar,
  output [3:0] out_9,
  output signe_minus
);

  wire decodeur_1_a, decodeur_1_b, decodeur_1_c, decodeur_1_d;
  wire [3:0] add_sub_1_s, and_4bit_1_and, nona_1_minus_a, or_4bit_1_or, xor_4bit_1_xor;

  ADD_SUB add_sub_1 (.s(add_sub_1_s), .signe(signe_minus), .A(A), .plus_OU_minus(decodeur_1_d), .B(B));
  OR_4BIT or_4bit_1 (.A(A), .B(B), .OR(or_4bit_1_or));
  AND_4BIT and_4bit_1 (.A(A), .B(B), .AND(and_4bit_1_and));
  XOR_4BIT xor_4bit_1 (.A(A), .B(B), .XOR(xor_4bit_1_xor));
  nonA nona_1 (.A(A), .minus_A(nona_1_minus_a));
  decodeur decodeur_1 (
    .OR(OR), .AND(AND), .XOR(XOR), .Abar(Abar), .ADD(ADD), .SUB(SUB), .a(decodeur_1_a), .b(decodeur_1_b),
    .c(decodeur_1_c), .d(decodeur_1_d));
  MUX mux_1 (
    .in_1(or_4bit_1_or), .in_2(and_4bit_1_and), .in_3(xor_4bit_1_xor), .in_4(nona_1_minus_a),
    .in_5(add_sub_1_s), .in_6(decodeur_1_a), .in_7(decodeur_1_b), .in_8(decodeur_1_c), .out_9(out_9));
endmodule
