// Logisim project clock.circ as structural Verilog: 17 circuits, main circuit CPT10
module CPT10 (
  input  CLOCK,
  output _0,
  output _1,
  output _2,
  output _3,
  output RESERT
);

  wire j_k_ff_1_qn, j_k_ff_2_qn, j_k_ff_3_qn;

  J_K_Flip_Flop j_k_ff_1 (
    .J(1'b1), .clk(CLOCK), .K(1'b1), .Q(_0), .Qn(j_k_ff_1_qn), .reset(RESERT));  // open: preset, en
  J_K_Flip_Flop j_k_ff_2 (
    .J(1'b1), .clk(j_k_ff_1_qn), .K(1'b1), .Q(_1), .Qn(j_k_ff_2_qn), .reset(RESERT));  // open: preset, en
  J_K_Flip_Flop j_k_ff_3 (
    .J(1'b1), .clk(j_k_ff_2_qn), .K(1'b1), .Q(_2), .Qn(j_k_ff_3_qn), .reset(RESERT));  // open: preset, en
  J_K_Flip_Flop j_k_ff_4 (.J(1'b1), .clk(j_k_ff_3_qn), .K(1'b1), .Q(_3), .reset(RESERT));  // open: Qn, preset, en
  and and_1 (RESERT, _1, _3);
endmodule

module ms (
  input  \resetforcé ,
  input  CLOCK,
  output [3:0] ms1,
  output [3:0] ms0,
  output resert
);

  wire and_1_out, and_2_out, and_3_out, j_k_ff_1_qn, j_k_ff_2_qn, j_k_ff_3_qn, j_k_ff_4_qn, j_k_ff_5_qn,
       j_k_ff_6_qn, or_1_out, or_2_out;

  Clock clock_1 ();  // open: out
  J_K_Flip_Flop j_k_ff_1 (
    .J(1'b1), .clk(and_2_out), .K(1'b1), .Q(ms1[0]), .Qn(j_k_ff_1_qn), .reset(or_1_out));  // open: preset, en
  J_K_Flip_Flop j_k_ff_2 (
    .J(1'b1), .clk(CLOCK), .K(1'b1), .Q(ms0[0]), .Qn(j_k_ff_2_qn), .reset(or_2_out));  // open: preset, en
  J_K_Flip_Flop j_k_ff_3 (
    .J(1'b1), .clk(j_k_ff_1_qn), .K(1'b1), .Q(ms1[1]), .Qn(j_k_ff_3_qn), .reset(or_1_out));  // open: preset, en
  J_K_Flip_Flop j_k_ff_4 (
    .J(1'b1), .clk(j_k_ff_2_qn), .K(1'b1), .Q(ms0[1]), .Qn(j_k_ff_4_qn), .reset(or_2_out));  // open: preset, en
  J_K_Flip_Flop j_k_ff_5 (
    .J(1'b1), .clk(j_k_ff_3_qn), .K(1'b1), .Q(ms1[2]), .Qn(j_k_ff_5_qn), .reset(or_1_out));  // open: preset, en
  J_K_Flip_Flop j_k_ff_6 (
    .J(1'b1), .clk(j_k_ff_4_qn), .K(1'b1), .Q(ms0[2]), .Qn(j_k_ff_6_qn), .reset(or_2_out));  // open: preset, en
  J_K_Flip_Flop j_k_ff_7 (.J(1'b1), .clk(j_k_ff_5_qn), .K(1'b1), .Q(ms1[3]), .reset(or_1_out));  // open: Qn, preset, en
  J_K_Flip_Flop j_k_ff_8 (.J(1'b1), .clk(j_k_ff_6_qn), .K(1'b1), .Q(ms0[3]), .reset(or_2_out));  // open: Qn, preset, en
  and and_1 (and_1_out, ms1[1], ms1[3]);
  or or_1 (or_1_out, and_1_out, \resetforcé );
  and and_2 (and_2_out, ms0[1], ms0[3]);
  or or_2 (or_2_out, and_2_out, \resetforcé );
  and and_3 (and_3_out, ms1[0], ms1[3]);
  Hex_Digit_Display hex_digit_display_1 (.value(ms1));  // open: dp
  and and_4 (resert, and_3_out, ms0[3], ms0[0]);
  Hex_Digit_Display hex_digit_display_2 (.value(ms0));  // open: dp
endmodule

module CTP_SECD (
  input  restforc,
  input  [2:0] sc1,
  input  CLOCK,
  input  [3:0] sc0,
  output [3:0] SCD1,
  output resert,
  output [3:0] SCD0,
  output points
);

  wire and_1_out, and_2_out, and_3_out, j_k_ff_1_qn, j_k_ff_2_qn, j_k_ff_3_qn, j_k_ff_4_qn, j_k_ff_5_qn,
       j_k_ff_6_qn, or_1_out, or_2_out;

  J_K_Flip_Flop j_k_ff_1 (
    .J(1'b1), .clk(or_1_out), .K(1'b1), .Q(SCD1[0]), .Qn(j_k_ff_1_qn), .preset(sc1[0]), .reset(or_2_out));  // open: en
  J_K_Flip_Flop j_k_ff_2 (
    .J(1'b1), .clk(CLOCK), .K(1'b1), .Q(points), .Qn(j_k_ff_2_qn), .preset(sc0[0]), .reset(or_1_out));  // open: en
  J_K_Flip_Flop j_k_ff_3 (
    .J(1'b1), .clk(j_k_ff_2_qn), .K(1'b1), .Q(SCD0[1]), .Qn(j_k_ff_3_qn), .preset(sc0[1]), .reset(or_1_out));  // open: en
  J_K_Flip_Flop j_k_ff_4 (
    .J(1'b1), .clk(j_k_ff_1_qn), .K(1'b1), .Q(SCD1[1]), .Qn(j_k_ff_4_qn), .preset(sc1[1]), .reset(or_2_out));  // open: en
  J_K_Flip_Flop j_k_ff_5 (
    .J(1'b1), .clk(j_k_ff_4_qn), .K(1'b1), .Q(SCD1[2]), .Qn(j_k_ff_5_qn), .preset(sc1[2]), .reset(or_2_out));  // open: en
  J_K_Flip_Flop j_k_ff_6 (
    .J(1'b1), .clk(j_k_ff_3_qn), .K(1'b1), .Q(SCD0[2]), .Qn(j_k_ff_6_qn), .preset(sc0[2]), .reset(or_1_out));  // open: en
  J_K_Flip_Flop j_k_ff_7 (
    .J(1'b1), .clk(j_k_ff_5_qn), .K(1'b1), .Q(SCD1[3]), .reset(or_2_out));  // open: Qn, preset, en
  J_K_Flip_Flop j_k_ff_8 (
    .J(1'b1), .clk(j_k_ff_6_qn), .K(1'b1), .Q(SCD0[3]), .preset(sc0[3]), .reset(or_1_out));  // open: Qn, en
  and and_1 (and_1_out, SCD1[1], SCD1[2]);
  and and_2 (and_2_out, points, SCD0[3]);
  or or_1 (or_1_out, and_2_out, restforc);
  or or_2 (or_2_out, restforc, and_1_out);
  and and_3 (and_3_out, SCD1[2], SCD1[0]);
  and and_4 (resert, and_3_out, and_2_out);
  Hex_Digit_Display hex_digit_display_1 (.value(SCD1));  // open: dp
  Hex_Digit_Display hex_digit_display_2 (.value({SCD0[3:1], points}));  // open: dp

  assign SCD0[0] = points;
endmodule

module HOURES (
  input  arretforc,
  input  [1:0] _1,
  input  clock,
  input  [3:0] _0,
  output [3:0] hrs1,
  output resert,
  output [3:0] hrs0
);

  wire and_1_out, and_2_out, and_3_out, j_k_ff_1_qn, j_k_ff_2_qn, j_k_ff_3_qn, j_k_ff_5_qn, j_k_ff_6_qn,
       j_k_ff_7_qn, or_1_out, or_2_out, or_3_out;

  J_K_Flip_Flop j_k_ff_1 (
    .J(1'b1), .clk(or_2_out), .K(1'b1), .Q(hrs1[0]), .Qn(j_k_ff_1_qn), .preset(_1[0]), .reset(or_1_out));  // open: en
  J_K_Flip_Flop j_k_ff_2 (
    .J(1'b1), .clk(j_k_ff_1_qn), .K(1'b1), .Q(hrs1[1]), .Qn(j_k_ff_2_qn), .preset(_1[1]), .reset(or_1_out));  // open: en
  J_K_Flip_Flop j_k_ff_3 (
    .J(1'b1), .clk(j_k_ff_2_qn), .K(1'b1), .Q(hrs1[2]), .Qn(j_k_ff_3_qn), .reset(or_1_out));  // open: preset, en
  J_K_Flip_Flop j_k_ff_4 (
    .J(1'b1), .clk(j_k_ff_3_qn), .K(1'b1), .Q(hrs1[3]), .reset(or_1_out));  // open: Qn, preset, en
  and and_1 (and_1_out, hrs1[0], hrs1[1]);
  J_K_Flip_Flop j_k_ff_5 (
    .J(1'b1), .clk(clock), .K(1'b1), .Q(hrs0[0]), .Qn(j_k_ff_5_qn), .preset(_0[0]), .reset(or_3_out));  // open: en
  or or_1 (or_1_out, and_1_out, arretforc);
  J_K_Flip_Flop j_k_ff_6 (
    .J(1'b1), .clk(j_k_ff_5_qn), .K(1'b1), .Q(hrs0[1]), .Qn(j_k_ff_6_qn), .preset(_0[1]), .reset(or_3_out));  // open: en
  J_K_Flip_Flop j_k_ff_7 (
    .J(1'b1), .clk(j_k_ff_6_qn), .K(1'b1), .Q(hrs0[2]), .Qn(j_k_ff_7_qn), .preset(_0[2]), .reset(or_3_out));  // open: en
  J_K_Flip_Flop j_k_ff_8 (
    .J(1'b1), .clk(j_k_ff_7_qn), .K(1'b1), .Q(hrs0[3]), .preset(_0[3]), .reset(or_3_out));  // open: Qn, en
  and and_2 (and_2_out, hrs1[1], hrs0[2]);
  and and_3 (and_3_out, hrs0[1], hrs0[3]);
  or or_2 (or_2_out, and_2_out, and_3_out);
  or or_3 (or_3_out, or_2_out, arretforc);
  and and_4 (resert, hrs1[1], or_2_out);
endmodule

module jours (
  input  resetforc,
  input  [1:0] _1,
  input  clock,
  input  [3:0] _0,
  output [3:0] jrs1,
  output [3:0] jrs0,
  output resert,
  output xx
);

  wire and_1_out, and_2_out, and_3_out, and_4_out, j_k_ff_1_qn, j_k_ff_2_qn, j_k_ff_3_qn, j_k_ff_4_qn,
       j_k_ff_5_qn, j_k_ff_6_qn, not_1_out, or_1_out, or_2_out, or_3_out;
  wire [3:0] bit_extender_1_out, j_k_ff_2_q;

  J_K_Flip_Flop j_k_ff_1 (
    .J(1'b1), .clk(or_2_out), .K(1'b1), .Q(jrs1[0]), .Qn(j_k_ff_1_qn), .preset(_1[0]), .reset(or_1_out));  // open: en
  J_K_Flip_Flop j_k_ff_2 (
    .J(1'b1), .clk(clock), .K(1'b1), .Q(j_k_ff_2_q[0]), .Qn(j_k_ff_2_qn), .preset(_0[0]), .reset(or_2_out));  // open: en
  J_K_Flip_Flop j_k_ff_3 (
    .J(1'b1), .clk(j_k_ff_1_qn), .K(1'b1), .Q(jrs1[1]), .Qn(j_k_ff_3_qn), .preset(_1[1]), .reset(or_1_out));  // open: en
  J_K_Flip_Flop j_k_ff_4 (
    .J(1'b1), .clk(j_k_ff_2_qn), .K(1'b1), .Q(j_k_ff_2_q[1]), .Qn(j_k_ff_4_qn), .preset(_0[1]),
    .reset(or_2_out));  // open: en
  J_K_Flip_Flop j_k_ff_5 (
    .J(1'b1), .clk(j_k_ff_3_qn), .K(1'b1), .Q(jrs1[2]), .Qn(j_k_ff_5_qn), .reset(or_1_out));  // open: preset, en
  J_K_Flip_Flop j_k_ff_6 (
    .J(1'b1), .clk(j_k_ff_4_qn), .K(1'b1), .Q(j_k_ff_2_q[2]), .Qn(j_k_ff_6_qn), .preset(_0[2]),
    .reset(or_2_out));  // open: en
  and and_1 (and_1_out, jrs1[2], jrs1[2]);
  J_K_Flip_Flop j_k_ff_7 (
    .J(1'b1), .clk(j_k_ff_5_qn), .K(1'b1), .Q(jrs1[3]), .reset(or_1_out));  // open: Qn, preset, en
  J_K_Flip_Flop j_k_ff_8 (
    .J(1'b1), .clk(j_k_ff_6_qn), .K(1'b1), .Q(j_k_ff_2_q[3]), .preset(_0[3]), .reset(or_2_out));  // open: Qn, en
  or or_1 (or_1_out, and_1_out, resetforc);
  and and_2 (and_2_out, j_k_ff_2_q[0], j_k_ff_2_q[3]);
  or or_2 (or_2_out, resetforc, or_3_out);
  or or_3 (or_3_out, and_2_out, and_4_out);
  and and_3 (and_3_out, jrs1[1], jrs1[0]);
  and and_4 (and_4_out, j_k_ff_2_q[0], and_3_out);
  not not_1 (not_1_out, jrs1[0]);
  assign bit_extender_1_out = {{3{1'b0}}, not_1_out};  // Bit_Extender bit_extender_1
  Adder #(.width(4)) adder_1 (.a(bit_extender_1_out), .b(j_k_ff_2_q), .out(jrs0));  // open: cin, cout
  and and_5 (resert, and_4_out, and_3_out);

  assign xx = clock;
endmodule

module mois (
  input  resetforce,
  input  _1,
  input  CLOCK,
  input  [3:0] _0,
  output [3:0] mois1,
  output resert,
  output [3:0] mois0
);

  wire and_1_out, and_2_out, and_3_out, j_k_ff_1_qn, j_k_ff_2_qn, j_k_ff_3_qn, j_k_ff_4_qn, j_k_ff_5_qn,
       j_k_ff_6_qn, not_1_out, or_1_out, or_2_out, or_3_out;
  wire [3:0] bit_extender_1_out, j_k_ff_2_q;

  J_K_Flip_Flop j_k_ff_1 (
    .J(1'b1), .clk(or_2_out), .K(1'b1), .Q(mois1[0]), .Qn(j_k_ff_1_qn), .preset(_1), .reset(or_1_out));  // open: en
  J_K_Flip_Flop j_k_ff_2 (
    .J(1'b1), .clk(CLOCK), .K(1'b1), .Q(j_k_ff_2_q[0]), .Qn(j_k_ff_2_qn), .preset(_0[0]), .reset(or_3_out));  // open: en
  J_K_Flip_Flop j_k_ff_3 (
    .J(1'b1), .clk(j_k_ff_1_qn), .K(1'b1), .Q(mois1[1]), .Qn(j_k_ff_3_qn), .reset(or_1_out));  // open: preset, en
  J_K_Flip_Flop j_k_ff_4 (
    .J(1'b1), .clk(j_k_ff_2_qn), .K(1'b1), .Q(j_k_ff_2_q[1]), .Qn(j_k_ff_4_qn), .preset(_0[1]),
    .reset(or_3_out));  // open: en
  J_K_Flip_Flop j_k_ff_5 (
    .J(1'b1), .clk(j_k_ff_3_qn), .K(1'b1), .Q(mois1[2]), .Qn(j_k_ff_5_qn), .reset(or_1_out));  // open: preset, en
  J_K_Flip_Flop j_k_ff_6 (
    .J(1'b1), .clk(j_k_ff_4_qn), .K(1'b1), .Q(j_k_ff_2_q[2]), .Qn(j_k_ff_6_qn), .preset(_0[2]),
    .reset(or_3_out));  // open: en
  J_K_Flip_Flop j_k_ff_7 (
    .J(1'b1), .clk(j_k_ff_5_qn), .K(1'b1), .Q(mois1[3]), .reset(or_1_out));  // open: Qn, preset, en
  J_K_Flip_Flop j_k_ff_8 (
    .J(1'b1), .clk(j_k_ff_6_qn), .K(1'b1), .Q(j_k_ff_2_q[3]), .preset(_0[3]), .reset(or_3_out));  // open: Qn, en
  and and_1 (and_1_out, mois1[1], mois1[1]);
  or or_1 (or_1_out, and_1_out, resetforce);
  or or_2 (or_2_out, and_2_out, and_3_out);
  or or_3 (or_3_out, resetforce, or_2_out);
  and and_2 (and_2_out, j_k_ff_2_q[0], j_k_ff_2_q[3]);
  and and_3 (and_3_out, j_k_ff_2_q[0], j_k_ff_2_q[1], mois1[0]);
  not not_1 (not_1_out, mois1[0]);
  and and_4 (resert, and_1_out, or_2_out);
  assign bit_extender_1_out = {{3{1'b0}}, not_1_out};  // Bit_Extender bit_extender_1
  Adder #(.width(4)) adder_1 (.a(bit_extender_1_out), .b(j_k_ff_2_q), .out(mois0));  // open: cin, cout
endmodule

module afich_jrs (
  input  [5:0] in_1,
  input  [5:0] in_2,
  input  [5:0] in_3,
  input  [5:0] in_4,
  input  [5:0] in_5,
  input  [5:0] in_6,
  input  [5:0] in_7,
  input  [5:0] in_8,
  input  [5:0] in_9,
  input  [5:0] in_10,
  input  [5:0] in_11,
  input  [5:0] in_12,
  input  [5:0] in_13,
  input  [5:0] in_14,
  input  [5:0] in_15,
  input  [5:0] in_16,
  input  [5:0] in_17,
  input  [5:0] in_18,
  input  [5:0] in_19,
  input  [5:0] in_20,
  input  [5:0] in_21,
  input  [5:0] in_22,
  input  [5:0] in_23,
  input  [5:0] in_24,
  input  [5:0] in_25,
  input  [5:0] in_26,
  input  [5:0] in_27,
  input  [5:0] in_28,
  input  [5:0] in_29,
  input  [5:0] in_30,
  input  [5:0] in_31,
  input  [5:0] in_32,
  input  [5:0] in_33,
  input  [5:0] in_34,
  input  [5:0] in_35,
  input  [5:0] in_36,
  input  [5:0] in_37,
  input  [5:0] in_38,
  input  [5:0] in_39,
  input  [5:0] in_40,
  input  [5:0] in_41,
  input  [5:0] in_42,
  input  [5:0] in_43,
  input  [5:0] in_44,
  input  [5:0] in_45,
  input  [5:0] in_46,
  input  [5:0] in_47,
  input  [5:0] in_48,
  input  [5:0] in_49,
  input  [5:0] in_50,
  input  [5:0] in_51,
  input  [5:0] in_52,
  input  [5:0] in_53,
  input  [5:0] in_54,
  input  [5:0] in_55,
  input  [5:0] in_56,
  input  [5:0] in_57,
  input  [5:0] in_58,
  input  [5:0] in_59,
  input  [5:0] in_60,
  input  [5:0] in_61,
  input  [5:0] in_62,
  input  [5:0] in_63,
  input  [5:0] in_64,
  input  [5:0] in_65,
  input  [5:0] in_66,
  input  [5:0] in_67,
  input  [5:0] in_68,
  input  [5:0] in_69,
  input  [5:0] in_70,
  input  [5:0] in_71,
  input  [5:0] in_72,
  input  [5:0] in_73,
  input  [5:0] in_74,
  input  [5:0] in_75,
  input  [5:0] in_76,
  input  [5:0] in_77,
  input  [5:0] in_78,
  input  [5:0] in_79,
  input  [5:0] in_80,
  input  [5:0] in_81,
  input  [5:0] in_82,
  input  [5:0] in_83,
  input  [5:0] in_84,
  input  [5:0] in_85,
  input  [5:0] in_86,
  input  [5:0] in_87,
  input  [5:0] in_88,
  input  [5:0] in_89,
  input  [5:0] in_90,
  input  [5:0] in_91,
  input  [5:0] in_92,
  input  [5:0] in_93,
  input  [5:0] in_94,
  input  [5:0] in_95,
  input  [5:0] in_96,
  input  [5:0] in_97,
  input  [5:0] in_98,
  input  [5:0] in_99,
  input  [5:0] in_100,
  input  [5:0] in_101,
  input  [5:0] in_102,
  input  [5:0] in_103,
  input  [5:0] in_104,
  input  [5:0] in_105,
  input  [5:0] in_106,
  input  [5:0] in_107,
  input  [5:0] in_108,
  input  [5:0] in_109,
  input  [5:0] in_110,
  input  [5:0] in_111,
  input  [5:0] in_112,
  input  [5:0] in_113,
  input  [5:0] in_114,
  input  [5:0] in_115,
  input  [5:0] in_116,
  output [5:0] out_117,
  output [5:0] out_118,
  output [5:0] out_119,
  output [5:0] out_120,
  output [5:0] out_121,
  output [5:0] out_122,
  output [5:0] out_123,
  output [5:0] out_124,
  output [5:0] out_125,
  output [5:0] out_126,
  output [5:0] out_127,
  output [5:0] out_128,
  output [5:0] out_129,
  output [5:0] out_130,
  output [5:0] out_131,
  output [5:0] out_132,
  output [5:0] out_133,
  output [5:0] out_134,
  output [5:0] out_135,
  output [5:0] out_136,
  output [5:0] out_137,
  output [5:0] out_138,
  output [5:0] out_139,
  output [5:0] out_140,
  output [5:0] out_141,
  output [5:0] out_142,
  output [5:0] out_143,
  output [5:0] out_144,
  output [5:0] out_145,
  output [5:0] out_146,
  output [5:0] out_147,
  output [5:0] out_148,
  output [5:0] out_149,
  output [5:0] out_150,
  output [5:0] out_151,
  output [5:0] out_152,
  output [5:0] out_153,
  output [5:0] out_154,
  output [5:0] out_155,
  output [5:0] out_156,
  output [5:0] out_157,
  output [5:0] out_158,
  output [5:0] out_159,
  output [5:0] out_160,
  output [5:0] out_161,
  output [5:0] out_162,
  output [5:0] out_163,
  output [5:0] out_164,
  output [5:0] out_165,
  output [5:0] out_166,
  output [5:0] out_167,
  output [5:0] out_168,
  output [5:0] out_169,
  output [5:0] out_170,
  output [5:0] out_171,
  output [5:0] out_172,
  output [5:0] out_173,
  output [5:0] out_174,
  output [5:0] out_175,
  output [5:0] out_176,
  output [5:0] out_177,
  output [5:0] out_178,
  output [5:0] out_179,
  output [5:0] out_180,
  output [5:0] out_181,
  output [5:0] out_182,
  output [5:0] out_183,
  output [5:0] out_184,
  output [5:0] out_185,
  output [5:0] out_186,
  output [5:0] out_187,
  output [5:0] out_188,
  output [5:0] out_189,
  output [5:0] out_190,
  output [5:0] out_191,
  output [5:0] out_192,
  output [5:0] out_193,
  output [5:0] out_194,
  output [5:0] out_195,
  output [5:0] out_196,
  output [5:0] out_197,
  output [5:0] out_198,
  output [5:0] out_199,
  output [5:0] out_200,
  output [5:0] out_201,
  output [5:0] out_202,
  output [5:0] out_203,
  output [5:0] out_204,
  output [5:0] out_205,
  output [5:0] out_206,
  output [5:0] out_207,
  output [5:0] out_208,
  output [5:0] out_209,
  output [5:0] out_210,
  output [5:0] out_211,
  output [5:0] out_212,
  output [5:0] out_213,
  output [5:0] out_214,
  output [5:0] out_215,
  output [5:0] out_216,
  output [5:0] out_217,
  output [5:0] out_218,
  output [5:0] out_219,
  output [5:0] out_220,
  output [5:0] out_221,
  output [5:0] out_222,
  output [5:0] out_223,
  output [5:0] out_224,
  output [5:0] out_225,
  output [5:0] out_226,
  output [5:0] out_227,
  output [5:0] out_228,
  output [5:0] out_229,
  output [5:0] out_230,
  output [5:0] out_231,
  output [5:0] out_232,
  output [5:0] out_233,
  output [5:0] out_234,
  output [5:0] out_235,
  output [5:0] out_236,
  output [5:0] out_237,
  output [5:0] out_238,
  output [5:0] out_239,
  output [5:0] out_240,
  output [5:0] out_241,
  output [5:0] out_242,
  output [5:0] out_243,
  output [5:0] out_244,
  output [5:0] out_245,
  output [5:0] out_246,
  output [5:0] out_247,
  output [5:0] out_248,
  output [5:0] out_249,
  output [5:0] out_250,
  output [5:0] out_251,
  output [5:0] out_252,
  output [5:0] out_253,
  output [5:0] out_254,
  output [5:0] out_255,
  output [5:0] out_256,
  output [5:0] out_257,
  output [5:0] out_258,
  output [5:0] out_259,
  output [5:0] out_260,
  output [5:0] out_261,
  output [5:0] out_262,
  output [5:0] out_263,
  output [5:0] out_264,
  output [5:0] out_265,
  output [5:0] out_266,
  output [5:0] out_267,
  output [5:0] out_268,
  output [5:0] out_269,
  output [5:0] out_270,
  output [5:0] out_271,
  output [5:0] out_272,
  output [5:0] out_273,
  output [5:0] out_274,
  output [5:0] out_275,
  output [5:0] out_276,
  output [5:0] out_277,
  output [5:0] out_278,
  output [5:0] out_279,
  output [5:0] out_280,
  output [5:0] out_281,
  output [5:0] out_282,
  output [5:0] out_283,
  output [5:0] out_284,
  output [5:0] out_285,
  output [5:0] out_286
);

  wire not_4_out, not_8_out;
  wire [5:0] bit_extender_2_out;

  assign {{3{out_177[5]}}, out_187[2:1], out_177[5]} = {{5{1'b0}}, not_4_out};  // Bit_Extender bit_extender_1
  assign out_173 = ~{{3{out_177[5]}}, out_187[2:1], out_177[5]};  // NOT_Gate not_1, 6 bits wide
  assign out_190 = ~{{3{out_177[5]}}, out_187[2:1], out_177[5]};  // NOT_Gate not_2, 6 bits wide
  assign out_208 = ~{{3{out_177[5]}}, out_187[2:1], out_177[5]};  // NOT_Gate not_3, 6 bits wide
  not not_4 (not_4_out, 1'b1);
  DotMatrix #(.matrixcols(17), .matrixrows(6)) dotmatrix_1 (
    .col0(out_173), .col1({out_177[5], 1'b1, {2{out_177[5]}}, 1'b1, out_177[5]}),
    .col2({out_177[5], 1'b1, {2{out_177[5]}}, 1'b1, out_177[5]}), .col3({out_177[5], 4'b1111, out_177[5]}),
    .col4({{3{out_177[5]}}, out_187[2:1], out_177[5]}), .col5(out_190),
    .col6({1'b1, out_177[5], 1'b1, {2{out_177[5]}}, 1'b1}),
    .col7({1'b1, out_177[5], 1'b1, {2{out_177[5]}}, 1'b1}),
    .col8({{3{out_177[5]}}, out_187[2:1], out_177[5]}), .col9({{3{out_177[5]}}, out_187[2:1], out_177[5]}),
    .col10({{3{out_177[5]}}, out_187[2:1], out_177[5]}), .col11(out_208),
    .col12({1'b1, {4{out_177[5]}}, 1'b1}), .col13({1'b1, {4{out_177[5]}}, 1'b1}),
    .col14({1'b1, {4{out_177[5]}}, 1'b1}), .col15({{3{out_177[5]}}, out_187[2:1], out_177[5]}),
    .col16({{3{out_177[5]}}, out_187[2:1], out_177[5]}));
  DotMatrix #(.matrixcols(17), .matrixrows(6)) dotmatrix_2 (
    .col0(in_50), .col1(in_52), .col2(in_54), .col3(in_58), .col4(in_62), .col5(in_66), .col6(in_70),
    .col7(in_74), .col8(in_78), .col9(in_82), .col10(in_86), .col11(in_90), .col12(in_94), .col13(in_98),
    .col14(in_102), .col15(in_106), .col16(in_110));
  assign bit_extender_2_out = {{5{1'b0}}, not_8_out};  // Bit_Extender bit_extender_2
  assign out_151 = ~bit_extender_2_out;  // NOT_Gate not_5, 6 bits wide
  assign out_157 = ~bit_extender_2_out;  // NOT_Gate not_6, 6 bits wide
  assign out_161 = ~bit_extender_2_out;  // NOT_Gate not_7, 6 bits wide
  not not_8 (not_8_out, 1'b1);
  DotMatrix #(.matrixcols(17), .matrixrows(6)) dotmatrix_3 (
    .col0(out_151), .col1(in_1), .col2(in_2), .col3(in_5), .col4(in_8), .col5(in_11), .col6(out_157),
    .col7(in_16), .col8(in_19), .col9(in_22), .col10(out_161), .col11(in_26), .col12(in_29), .col13(in_32),
    .col14(in_36), .col15(in_39), .col16(in_42));
  DotMatrix #(.matrixcols(17), .matrixrows(6)) dotmatrix_4 (
    .col0(in_49), .col1(in_51), .col2(in_53), .col3(in_57), .col4(in_61), .col5(in_65), .col6(in_69),
    .col7(in_73), .col8(in_77), .col9(in_81), .col10(in_85), .col11(in_88), .col12(in_92), .col13(in_96),
    .col14(in_101), .col15(in_105), .col16(in_109));
  assign out_124 = {{5{1'b0}}, out_118[5]};  // Bit_Extender bit_extender_3
  not not_9 (out_118[5], 1'b1);
  DotMatrix #(.matrixcols(17), .matrixrows(6)) dotmatrix_5 (
    .col0({{4{out_118[5]}}, 2'b11}), .col1({1'b1, {4{out_118[5]}}, 1'b1}), .col2({6{1'b1}}), .col3(out_124),
    .col4({6{1'b1}}), .col5({1'b1, out_124[5], 1'b1, {3{out_124[5]}}}),
    .col6({1'b1, out_124[5], 1'b1, {3{out_124[5]}}}), .col7({6{1'b1}}), .col8(out_124), .col9(out_124),
    .col10({6{1'b1}}), .col11({1'b1, {5{out_124[5]}}}), .col12({out_124[5], 2'b11, {3{out_124[5]}}}),
    .col13({{3{out_124[5]}}, 1'b1, {2{out_124[5]}}}), .col14({6{1'b1}}), .col15(out_124), .col16(out_124));
  DotMatrix #(.matrixcols(17), .matrixrows(6)) dotmatrix_6 (
    .col0(in_4), .col1(in_7), .col2(in_10), .col3(in_13), .col4(in_15), .col5(in_18), .col6(in_21),
    .col7(in_24), .col8(in_27), .col9(in_30), .col10(in_33), .col11(in_35), .col12(in_38), .col13(in_41),
    .col14(in_44), .col15(in_46), .col16(in_48));
  DotMatrix #(.matrixcols(17), .matrixrows(6)) dotmatrix_7 (
    .col0(in_56), .col1(in_60), .col2(in_64), .col3(in_68), .col4(in_72), .col5(in_76), .col6(in_80),
    .col7(in_84), .col8(in_89), .col9(in_93), .col10(in_97), .col11(in_100), .col12(in_104), .col13(in_108),
    .col14(in_112), .col15(in_114), .col16(in_116));
  assign out_123 = {{5{1'b0}}, out_119[4]};  // Bit_Extender bit_extender_4
  assign out_117 = ~out_123;  // NOT_Gate not_10, 6 bits wide
  assign out_125 = ~out_123;  // NOT_Gate not_11, 6 bits wide
  not not_12 (out_119[4], 1'b1);
  DotMatrix #(.matrixcols(17), .matrixrows(6)) dotmatrix_8 (
    .col0(out_117), .col1({1'b1, out_119[4], 1'b1, {3{out_119[4]}}}),
    .col2({1'b1, out_119[4], 1'b1, {3{out_119[4]}}}), .col3(out_123), .col4(out_125),
    .col5({out_125[5], {2{out_119[4]}}, out_125[5], out_119[4], out_125[5]}),
    .col6({out_125[5], {2{out_119[4]}}, out_125[5], out_119[4], out_125[5]}), .col7(out_123),
    .col8({out_125[5], {5{out_123[5]}}}), .col9({out_123[5], {2{out_125[5]}}, {3{out_123[5]}}}),
    .col10({{2{out_123[5]}}, {2{out_125[5]}}, {2{out_123[5]}}}), .col11({{4{out_123[5]}}, {2{out_125[5]}}}),
    .col12({{2{out_123[5]}}, {2{out_125[5]}}, {2{out_123[5]}}}),
    .col13({out_123[5], {2{out_125[5]}}, {3{out_123[5]}}}), .col14({out_125[5], {5{out_123[5]}}}),
    .col15(out_123), .col16(out_123));
  DotMatrix #(.matrixcols(17), .matrixrows(6)) dotmatrix_9 (
    .col0(in_3), .col1(in_6), .col2(in_9), .col3(in_12), .col4(in_14), .col5(in_17), .col6(in_20),
    .col7(in_23), .col8(in_25), .col9(in_28), .col10(in_31), .col11(in_34), .col12(in_37), .col13(in_40),
    .col14(in_43), .col15(in_45), .col16(in_47));
  DotMatrix #(.matrixcols(17), .matrixrows(6)) dotmatrix_10 (
    .col0(in_55), .col1(in_59), .col2(in_63), .col3(in_67), .col4(in_71), .col5(in_75), .col6(in_79),
    .col7(in_83), .col8(in_87), .col9(in_91), .col10(in_95), .col11(in_99), .col12(in_103), .col13(in_107),
    .col14(in_111), .col15(in_113), .col16(in_115));

  assign out_118[4:0] = {{3{out_118[5]}}, 2'b11};
  assign {out_119[5], out_119[3:0]} = {2'b11, {3{out_119[4]}}};
  assign out_120 = {1'b1, {4{out_118[5]}}, 1'b1};
  assign out_121 = {1'b1, out_119[4], 1'b1, {3{out_119[4]}}};
  assign out_122 = {6{1'b1}};
  assign out_126 = {6{1'b1}};
  assign out_127 = {out_125[5], {2{out_119[4]}}, out_125[5], out_119[4], out_125[5]};
  assign out_128 = {1'b1, out_124[5], 1'b1, {3{out_124[5]}}};
  assign out_129 = {out_125[5], {2{out_119[4]}}, out_125[5], out_119[4], out_125[5]};
  assign out_130 = {1'b1, out_124[5], 1'b1, {3{out_124[5]}}};
  assign out_131 = out_123;
  assign out_132 = {6{1'b1}};
  assign out_133 = {out_125[5], {5{out_123[5]}}};
  assign out_134 = out_124;
  assign out_135 = {out_123[5], {2{out_125[5]}}, {3{out_123[5]}}};
  assign out_136 = out_124;
  assign out_137 = {{2{out_123[5]}}, {2{out_125[5]}}, {2{out_123[5]}}};
  assign out_138 = {6{1'b1}};
  assign out_139 = {{4{out_123[5]}}, {2{out_125[5]}}};
  assign out_140 = {1'b1, {5{out_124[5]}}};
  assign out_141 = {{2{out_123[5]}}, {2{out_125[5]}}, {2{out_123[5]}}};
  assign out_142 = {out_124[5], 2'b11, {3{out_124[5]}}};
  assign out_143 = {out_123[5], {2{out_125[5]}}, {3{out_123[5]}}};
  assign out_144 = {{3{out_124[5]}}, 1'b1, {2{out_124[5]}}};
  assign out_145 = {out_125[5], {5{out_123[5]}}};
  assign out_146 = {6{1'b1}};
  assign out_147 = out_123;
  assign out_148 = out_124;
  assign out_149 = out_123;
  assign out_150 = out_124;
  assign out_152 = in_1;
  assign out_153 = in_2;
  assign out_154 = in_5;
  assign out_155 = in_8;
  assign out_156 = in_11;
  assign out_158 = in_16;
  assign out_159 = in_19;
  assign out_160 = in_22;
  assign out_162 = in_3;
  assign out_163 = in_26;
  assign out_164 = in_4;
  assign out_165 = in_6;
  assign out_166 = in_29;
  assign out_167 = in_7;
  assign out_168 = in_9;
  assign out_169 = in_32;
  assign out_170 = in_10;
  assign out_171 = in_12;
  assign out_172 = in_36;
  assign out_174 = in_13;
  assign out_175 = in_14;
  assign out_176 = in_39;
  assign out_177[4:0] = {1'b1, {2{out_177[5]}}, 1'b1, out_177[5]};
  assign out_178 = in_15;
  assign out_179 = in_17;
  assign out_180 = in_42;
  assign out_181 = {out_177[5], 1'b1, {2{out_177[5]}}, 1'b1, out_177[5]};
  assign out_182 = in_18;
  assign out_183 = in_20;
  assign out_184 = {out_177[5], 4'b1111, out_177[5]};
  assign out_185 = in_21;
  assign out_186 = in_23;
  assign {out_187[5:3], out_187[0]} = {4{out_177[5]}};
  assign out_188 = in_24;
  assign out_189 = in_25;
  assign out_191 = in_27;
  assign out_192 = in_28;
  assign out_193 = {1'b1, out_177[5], 1'b1, {2{out_177[5]}}, 1'b1};
  assign out_194 = in_30;
  assign out_195 = in_31;
  assign out_196 = {1'b1, out_177[5], 1'b1, {2{out_177[5]}}, 1'b1};
  assign out_197 = in_33;
  assign out_198 = in_34;
  assign out_199 = {{3{out_177[5]}}, out_187[2:1], out_177[5]};
  assign out_200 = in_35;
  assign out_201 = in_37;
  assign out_202 = {{3{out_177[5]}}, out_187[2:1], out_177[5]};
  assign out_203 = in_38;
  assign out_204 = in_40;
  assign out_205 = {{3{out_177[5]}}, out_187[2:1], out_177[5]};
  assign out_206 = in_41;
  assign out_207 = in_43;
  assign out_209 = in_44;
  assign out_210 = in_45;
  assign out_211 = {1'b1, {4{out_177[5]}}, 1'b1};
  assign out_212 = in_46;
  assign out_213 = in_47;
  assign out_214 = {1'b1, {4{out_177[5]}}, 1'b1};
  assign out_215 = in_48;
  assign out_216 = {1'b1, {4{out_177[5]}}, 1'b1};
  assign out_217 = {{3{out_177[5]}}, out_187[2:1], out_177[5]};
  assign out_218 = {{3{out_177[5]}}, out_187[2:1], out_177[5]};
  assign out_219 = in_49;
  assign out_220 = in_50;
  assign out_221 = in_51;
  assign out_222 = in_52;
  assign out_223 = in_53;
  assign out_224 = in_54;
  assign out_225 = in_57;
  assign out_226 = in_58;
  assign out_227 = in_61;
  assign out_228 = in_62;
  assign out_229 = in_65;
  assign out_230 = in_66;
  assign out_231 = in_69;
  assign out_232 = in_70;
  assign out_233 = in_73;
  assign out_234 = in_74;
  assign out_235 = in_77;
  assign out_236 = in_78;
  assign out_237 = in_81;
  assign out_238 = in_82;
  assign out_239 = in_85;
  assign out_240 = in_55;
  assign out_241 = in_86;
  assign out_242 = in_88;
  assign out_243 = in_56;
  assign out_244 = in_59;
  assign out_245 = in_90;
  assign out_246 = in_92;
  assign out_247 = in_60;
  assign out_248 = in_63;
  assign out_249 = in_94;
  assign out_250 = in_96;
  assign out_251 = in_64;
  assign out_252 = in_67;
  assign out_253 = in_98;
  assign out_254 = in_101;
  assign out_255 = in_68;
  assign out_256 = in_71;
  assign out_257 = in_102;
  assign out_258 = in_105;
  assign out_259 = in_72;
  assign out_260 = in_75;
  assign out_261 = in_106;
  assign out_262 = in_109;
  assign out_263 = in_76;
  assign out_264 = in_79;
  assign out_265 = in_110;
  assign out_266 = in_80;
  assign out_267 = in_83;
  assign out_268 = in_84;
  assign out_269 = in_87;
  assign out_270 = in_89;
  assign out_271 = in_91;
  assign out_272 = in_93;
  assign out_273 = in_95;
  assign out_274 = in_97;
  assign out_275 = in_99;
  assign out_276 = in_100;
  assign out_277 = in_103;
  assign out_278 = in_104;
  assign out_279 = in_107;
  assign out_280 = in_108;
  assign out_281 = in_111;
  assign out_282 = in_112;
  assign out_283 = in_113;
  assign out_284 = in_114;
  assign out_285 = in_115;
  assign out_286 = in_116;
endmodule

module lun (
  output [5:0] out_1,
  output [5:0] out_2,
  output [5:0] out_3,
  output [5:0] out_4,
  output [5:0] out_5,
  output [5:0] out_6,
  output [5:0] out_7,
  output [5:0] out_8,
  output [5:0] out_9,
  output [5:0] out_10,
  output [5:0] out_11,
  output [5:0] out_12,
  output [5:0] out_13,
  output [5:0] out_14,
  output [5:0] out_15,
  output [5:0] out_16,
  output [5:0] out_17
);

  assign out_5 = {{5{1'b0}}, out_2[5]};  // Bit_Extender bit_extender_1
  assign out_12 = ~out_5;  // NOT_Gate not_1, 6 bits wide
  assign out_16 = ~out_5;  // NOT_Gate not_2, 6 bits wide
  not not_3 (out_2[5], 1'b1);
  DotMatrix #(.matrixcols(17), .matrixrows(6)) dotmatrix_1 (
    .col0({6{1'b1}}), .col1({{5{out_2[5]}}, 1'b1}), .col2({{5{out_2[5]}}, 1'b1}),
    .col3({{5{out_2[5]}}, 1'b1}), .col4(out_5), .col5({out_2[5], {5{1'b1}}}), .col6({{5{out_2[5]}}, 1'b1}),
    .col7({{5{out_2[5]}}, 1'b1}), .col8({{5{out_2[5]}}, 1'b1}), .col9({out_2[5], {5{1'b1}}}), .col10(out_5),
    .col11(out_12), .col12({out_2[5], 1'b1, {4{out_2[5]}}}), .col13({{2{out_2[5]}}, 2'b11, {2{out_2[5]}}}),
    .col14({{4{out_2[5]}}, 1'b1, out_2[5]}), .col15(out_16), .col16(out_5));

  assign out_1 = {6{1'b1}};
  assign out_2[4:0] = {{4{out_2[5]}}, 1'b1};
  assign out_3 = {{5{out_2[5]}}, 1'b1};
  assign out_4 = {{5{out_2[5]}}, 1'b1};
  assign out_6 = {out_2[5], {5{1'b1}}};
  assign out_7 = {{5{out_2[5]}}, 1'b1};
  assign out_8 = {{5{out_2[5]}}, 1'b1};
  assign out_9 = {{5{out_2[5]}}, 1'b1};
  assign out_10 = {out_2[5], {5{1'b1}}};
  assign out_11 = out_5;
  assign out_13 = {out_2[5], 1'b1, {4{out_2[5]}}};
  assign out_14 = {{2{out_2[5]}}, 2'b11, {2{out_2[5]}}};
  assign out_15 = {{4{out_2[5]}}, 1'b1, out_2[5]};
  assign out_17 = out_5;
endmodule

module mard (
  output [5:0] out_1,
  output [5:0] out_2,
  output [5:0] out_3,
  output [5:0] out_4,
  output [5:0] out_5,
  output [5:0] out_6,
  output [5:0] out_7,
  output [5:0] out_8,
  output [5:0] out_9,
  output [5:0] out_10,
  output [5:0] out_11,
  output [5:0] out_12,
  output [5:0] out_13,
  output [5:0] out_14,
  output [5:0] out_15,
  output [5:0] out_16,
  output [5:0] out_17
);

  not not_1 (out_2[4], 1'b1);
  DotMatrix #(.matrixcols(17), .matrixrows(6)) dotmatrix_1 (
    .col0({6{1'b1}}), .col1({1'b1, {5{out_2[4]}}}), .col2({out_2[4], 1'b1, {4{out_2[4]}}}),
    .col3({1'b1, {5{out_2[4]}}}), .col4({6{1'b1}}), .col5({6{out_2[4]}}), .col6({6{1'b1}}),
    .col7({1'b1, out_2[4], 1'b1, {3{out_2[4]}}}), .col8({1'b1, out_2[4], 1'b1, {3{out_2[4]}}}),
    .col9({6{1'b1}}), .col10({6{out_2[4]}}), .col11({6{1'b1}}), .col12({1'b1, {5{out_2[4]}}}),
    .col13({1'b1, out_2[4], 2'b11, {2{out_2[4]}}}), .col14({3'b111, out_2[4], 2'b11}), .col15({6{out_2[4]}}),
    .col16({6{out_2[4]}}));

  assign out_1 = {6{1'b1}};
  assign {out_2[5], out_2[3:0]} = {1'b1, {4{out_2[4]}}};
  assign out_3 = {out_2[4], 1'b1, {4{out_2[4]}}};
  assign out_4 = {1'b1, {5{out_2[4]}}};
  assign out_5 = {6{1'b1}};
  assign out_6 = {6{out_2[4]}};
  assign out_7 = {6{1'b1}};
  assign out_8 = {1'b1, out_2[4], 1'b1, {3{out_2[4]}}};
  assign out_9 = {1'b1, out_2[4], 1'b1, {3{out_2[4]}}};
  assign out_10 = {6{1'b1}};
  assign out_11 = {6{out_2[4]}};
  assign out_12 = {6{1'b1}};
  assign out_13 = {1'b1, {5{out_2[4]}}};
  assign out_14 = {1'b1, out_2[4], 2'b11, {2{out_2[4]}}};
  assign out_15 = {3'b111, out_2[4], 2'b11};
  assign out_16 = {6{out_2[4]}};
  assign out_17 = {6{out_2[4]}};
endmodule

module mer (
  output [5:0] out_1,
  output [5:0] out_2,
  output [5:0] out_3,
  output [5:0] out_4,
  output [5:0] out_5,
  output [5:0] out_6,
  output [5:0] out_7,
  output [5:0] out_8,
  output [5:0] out_9,
  output [5:0] out_10,
  output [5:0] out_11,
  output [5:0] out_12,
  output [5:0] out_13,
  output [5:0] out_14,
  output [5:0] out_15,
  output [5:0] out_16,
  output [5:0] out_17
);

  not not_1 (out_2[5], 1'b1);
  DotMatrix #(.matrixcols(17), .matrixrows(6)) dotmatrix_1 (
    .col0({6{1'b1}}), .col1({out_2[5], 1'b1, {4{out_2[5]}}}), .col2({{2{out_2[5]}}, 1'b1, {3{out_2[5]}}}),
    .col3({out_2[5], 1'b1, {4{out_2[5]}}}), .col4({6{1'b1}}), .col5({6{out_2[5]}}), .col6({6{1'b1}}),
    .col7({1'b1, {2{out_2[5]}}, 1'b1, out_2[5], 1'b1}), .col8({1'b1, {2{out_2[5]}}, 1'b1, out_2[5], 1'b1}),
    .col9({1'b1, {4{out_2[5]}}, 1'b1}), .col10({6{out_2[5]}}), .col11({6{1'b1}}),
    .col12({1'b1, {5{out_2[5]}}}), .col13({1'b1, {2{out_2[5]}}, 1'b1, {2{out_2[5]}}}),
    .col14({1'b1, out_2[5], 1'b1, out_2[5], 1'b1, out_2[5]}), .col15({out_2[5], 1'b1, {3{out_2[5]}}, 1'b1}),
    .col16({6{out_2[5]}}));

  assign out_1 = {6{1'b1}};
  assign out_2[4:0] = {1'b1, {4{out_2[5]}}};
  assign out_3 = {{2{out_2[5]}}, 1'b1, {3{out_2[5]}}};
  assign out_4 = {out_2[5], 1'b1, {4{out_2[5]}}};
  assign out_5 = {6{1'b1}};
  assign out_6 = {6{out_2[5]}};
  assign out_7 = {6{1'b1}};
  assign out_8 = {1'b1, {2{out_2[5]}}, 1'b1, out_2[5], 1'b1};
  assign out_9 = {1'b1, {2{out_2[5]}}, 1'b1, out_2[5], 1'b1};
  assign out_10 = {1'b1, {4{out_2[5]}}, 1'b1};
  assign out_11 = {6{out_2[5]}};
  assign out_12 = {6{1'b1}};
  assign out_13 = {1'b1, {5{out_2[5]}}};
  assign out_14 = {1'b1, {2{out_2[5]}}, 1'b1, {2{out_2[5]}}};
  assign out_15 = {1'b1, out_2[5], 1'b1, out_2[5], 1'b1, out_2[5]};
  assign out_16 = {out_2[5], 1'b1, {3{out_2[5]}}, 1'b1};
  assign out_17 = {6{out_2[5]}};
endmodule

module jeu (
  output [5:0] out_1,
  output [5:0] out_2,
  output [5:0] out_3,
  output [5:0] out_4,
  output [5:0] out_5,
  output [5:0] out_6,
  output [5:0] out_7,
  output [5:0] out_8,
  output [5:0] out_9,
  output [5:0] out_10,
  output [5:0] out_11,
  output [5:0] out_12,
  output [5:0] out_13,
  output [5:0] out_14,
  output [5:0] out_15,
  output [5:0] out_16,
  output [5:0] out_17
);

  not not_1 (out_1[4], 1'b1);
  DotMatrix #(.matrixcols(17), .matrixrows(6)) dotmatrix_1 (
    .col0({1'b1, {4{out_1[4]}}, 1'b1}), .col1({1'b1, {4{out_1[4]}}, 1'b1}), .col2({6{1'b1}}),
    .col3({6{out_1[4]}}), .col4({6{1'b1}}), .col5({1'b1, out_1[4], 1'b1, {2{out_1[4]}}, 1'b1}),
    .col6({1'b1, out_1[4], 1'b1, {2{out_1[4]}}, 1'b1}), .col7({1'b1, {4{out_1[4]}}, 1'b1}),
    .col8({6{out_1[4]}}), .col9({6{1'b1}}), .col10({{5{out_1[4]}}, 1'b1}), .col11({{5{out_1[4]}}, 1'b1}),
    .col12({6{1'b1}}), .col13({6{out_1[4]}}), .col14({6{1'b1}}),
    .col15({out_1[4], 1'b1, {2{out_1[4]}}, 1'b1, out_1[4]}), .col16({out_1[4], 4'b1111, out_1[4]}));

  assign {out_1[5], out_1[3:0]} = {1'b1, {3{out_1[4]}}, 1'b1};
  assign out_2 = {1'b1, {4{out_1[4]}}, 1'b1};
  assign out_3 = {6{1'b1}};
  assign out_4 = {6{out_1[4]}};
  assign out_5 = {6{1'b1}};
  assign out_6 = {1'b1, out_1[4], 1'b1, {2{out_1[4]}}, 1'b1};
  assign out_7 = {1'b1, out_1[4], 1'b1, {2{out_1[4]}}, 1'b1};
  assign out_8 = {1'b1, {4{out_1[4]}}, 1'b1};
  assign out_9 = {6{out_1[4]}};
  assign out_10 = {6{1'b1}};
  assign out_11 = {{5{out_1[4]}}, 1'b1};
  assign out_12 = {{5{out_1[4]}}, 1'b1};
  assign out_13 = {6{1'b1}};
  assign out_14 = {6{out_1[4]}};
  assign out_15 = {6{1'b1}};
  assign out_16 = {out_1[4], 1'b1, {2{out_1[4]}}, 1'b1, out_1[4]};
  assign out_17 = {out_1[4], 4'b1111, out_1[4]};
endmodule

module ven (
  output [5:0] out_1,
  output [5:0] out_2,
  output [5:0] out_3,
  output [5:0] out_4,
  output [5:0] out_5,
  output [5:0] out_6,
  output [5:0] out_7,
  output [5:0] out_8,
  output [5:0] out_9,
  output [5:0] out_10,
  output [5:0] out_11,
  output [5:0] out_12,
  output [5:0] out_13,
  output [5:0] out_14,
  output [5:0] out_15,
  output [5:0] out_16,
  output [5:0] out_17
);

  not not_1 (out_1[3], 1'b1);
  DotMatrix #(.matrixcols(17), .matrixrows(6)) dotmatrix_1 (
    .col0({2'b11, {4{out_1[3]}}}), .col1({{2{out_1[3]}}, 2'b11, {2{out_1[3]}}}),
    .col2({{3{out_1[3]}}, 2'b11, out_1[3]}), .col3({{5{out_1[3]}}, 1'b1}),
    .col4({{3{out_1[3]}}, 2'b11, out_1[3]}), .col5({{2{out_1[3]}}, 2'b11, {2{out_1[3]}}}),
    .col6({2'b11, {4{out_1[3]}}}), .col7({6{out_1[3]}}), .col8({6{1'b1}}),
    .col9({1'b1, out_1[3], 1'b1, {2{out_1[3]}}, 1'b1}), .col10({1'b1, out_1[3], 1'b1, {2{out_1[3]}}, 1'b1}),
    .col11({1'b1, {4{out_1[3]}}, 1'b1}), .col12({6{out_1[3]}}), .col13({6{1'b1}}),
    .col14({{2{out_1[3]}}, 1'b1, {3{out_1[3]}}}), .col15({{3{out_1[3]}}, 1'b1, {2{out_1[3]}}}),
    .col16({6{1'b1}}));

  assign {out_1[5:4], out_1[2:0]} = {2'b11, {3{out_1[3]}}};
  assign out_2 = {{2{out_1[3]}}, 2'b11, {2{out_1[3]}}};
  assign out_3 = {{3{out_1[3]}}, 2'b11, out_1[3]};
  assign out_4 = {{5{out_1[3]}}, 1'b1};
  assign out_5 = {{3{out_1[3]}}, 2'b11, out_1[3]};
  assign out_6 = {{2{out_1[3]}}, 2'b11, {2{out_1[3]}}};
  assign out_7 = {2'b11, {4{out_1[3]}}};
  assign out_8 = {6{out_1[3]}};
  assign out_9 = {6{1'b1}};
  assign out_10 = {1'b1, out_1[3], 1'b1, {2{out_1[3]}}, 1'b1};
  assign out_11 = {1'b1, out_1[3], 1'b1, {2{out_1[3]}}, 1'b1};
  assign out_12 = {1'b1, {4{out_1[3]}}, 1'b1};
  assign out_13 = {6{out_1[3]}};
  assign out_14 = {6{1'b1}};
  assign out_15 = {{2{out_1[3]}}, 1'b1, {3{out_1[3]}}};
  assign out_16 = {{3{out_1[3]}}, 1'b1, {2{out_1[3]}}};
  assign out_17 = {6{1'b1}};
endmodule

module sam (
  output [5:0] out_1,
  output [5:0] out_2,
  output [5:0] out_3,
  output [5:0] out_4,
  output [5:0] out_5,
  output [5:0] out_6,
  output [5:0] out_7,
  output [5:0] out_8,
  output [5:0] out_9,
  output [5:0] out_10,
  output [5:0] out_11,
  output [5:0] out_12,
  output [5:0] out_13,
  output [5:0] out_14,
  output [5:0] out_15,
  output [5:0] out_16,
  output [5:0] out_17
);

  not not_1 (out_1[2], 1'b1);
  DotMatrix #(.matrixcols(17), .matrixrows(6)) dotmatrix_1 (
    .col0({3'b111, {2{out_1[2]}}, 1'b1}), .col1({1'b1, out_1[2], 1'b1, {2{out_1[2]}}, 1'b1}),
    .col2({1'b1, out_1[2], 1'b1, {2{out_1[2]}}, 1'b1}), .col3({1'b1, out_1[2], 4'b1111}),
    .col4({6{out_1[2]}}), .col5({6{1'b1}}), .col6({1'b1, out_1[2], 1'b1, {3{out_1[2]}}}),
    .col7({1'b1, out_1[2], 1'b1, {3{out_1[2]}}}), .col8({6{1'b1}}), .col9({6{out_1[2]}}), .col10({6{1'b1}}),
    .col11({1'b1, {5{out_1[2]}}}), .col12({out_1[2], 2'b11, {3{out_1[2]}}}),
    .col13({{3{out_1[2]}}, 1'b1, {2{out_1[2]}}}), .col14({3'b111, {3{out_1[2]}}}),
    .col15({1'b1, {5{out_1[2]}}}), .col16({6{1'b1}}));

  assign {out_1[5:3], out_1[1:0]} = {3'b111, out_1[2], 1'b1};
  assign out_2 = {1'b1, out_1[2], 1'b1, {2{out_1[2]}}, 1'b1};
  assign out_3 = {1'b1, out_1[2], 1'b1, {2{out_1[2]}}, 1'b1};
  assign out_4 = {1'b1, out_1[2], 4'b1111};
  assign out_5 = {6{out_1[2]}};
  assign out_6 = {6{1'b1}};
  assign out_7 = {1'b1, out_1[2], 1'b1, {3{out_1[2]}}};
  assign out_8 = {1'b1, out_1[2], 1'b1, {3{out_1[2]}}};
  assign out_9 = {6{1'b1}};
  assign out_10 = {6{out_1[2]}};
  assign out_11 = {6{1'b1}};
  assign out_12 = {1'b1, {5{out_1[2]}}};
  assign out_13 = {out_1[2], 2'b11, {3{out_1[2]}}};
  assign out_14 = {{3{out_1[2]}}, 1'b1, {2{out_1[2]}}};
  assign out_15 = {3'b111, {3{out_1[2]}}};
  assign out_16 = {1'b1, {5{out_1[2]}}};
  assign out_17 = {6{1'b1}};
endmodule

module dim (
  output [5:0] out_1,
  output [5:0] out_2,
  output [5:0] out_3,
  output [5:0] out_4,
  output [5:0] out_5,
  output [5:0] out_6,
  output [5:0] out_7,
  output [5:0] out_8,
  output [5:0] out_9,
  output [5:0] out_10,
  output [5:0] out_11,
  output [5:0] out_12,
  output [5:0] out_13,
  output [5:0] out_14,
  output [5:0] out_15,
  output [5:0] out_16,
  output [5:0] out_17
);

  assign out_4 = {{5{1'b0}}, out_2[5]};  // Bit_Extender bit_extender_1
  not not_1 (out_2[5], 1'b1);
  DotMatrix #(.matrixcols(17), .matrixrows(6)) dotmatrix_1 (
    .col0({6{1'b1}}), .col1({out_2[5], 1'b1, {3{out_2[5]}}, 1'b1}), .col2({{2{out_2[5]}}, 3'b111, out_2[5]}),
    .col3(out_4), .col4(out_4), .col5({out_2[5], {5{1'b1}}}), .col6(out_4), .col7(out_4), .col8({6{1'b1}}),
    .col9({out_2[5], 1'b1, {4{out_2[5]}}}), .col10({{2{out_2[5]}}, 2'b11, {2{out_2[5]}}}),
    .col11({out_2[5], 1'b1, {4{out_2[5]}}}), .col12({6{1'b1}}), .col13(out_4), .col14(out_4), .col15(out_4),
    .col16(out_4));

  assign out_1 = {6{1'b1}};
  assign out_2[4:0] = {1'b1, {3{out_2[5]}}, 1'b1};
  assign out_3 = {{2{out_2[5]}}, 3'b111, out_2[5]};
  assign out_5 = out_4;
  assign out_6 = {out_2[5], {5{1'b1}}};
  assign out_7 = out_4;
  assign out_8 = out_4;
  assign out_9 = {6{1'b1}};
  assign out_10 = {out_2[5], 1'b1, {4{out_2[5]}}};
  assign out_11 = {{2{out_2[5]}}, 2'b11, {2{out_2[5]}}};
  assign out_12 = {out_2[5], 1'b1, {4{out_2[5]}}};
  assign out_13 = {6{1'b1}};
  assign out_14 = out_4;
  assign out_15 = out_4;
  assign out_16 = out_4;
  assign out_17 = out_4;
endmodule

module deco_jrs (
  input  CLOCK,
  output [5:0] out_2,
  output [5:0] out_3,
  output [5:0] out_4,
  output [5:0] out_5,
  output [5:0] out_6,
  output [5:0] out_7,
  output [5:0] out_8,
  output [5:0] out_9,
  output [5:0] out_10,
  output [5:0] out_11,
  output [5:0] out_12,
  output [5:0] out_13,
  output [5:0] out_14,
  output [5:0] out_15,
  output [5:0] out_16,
  output [5:0] out_17,
  output [5:0] out_18
);

  wire and_1_out, j_k_ff_1_qn, j_k_ff_2_qn;
  wire [2:0] j_k_ff_1_q;
  wire [5:0] dim_1_out_1, dim_1_out_2, dim_1_out_3, dim_1_out_4, dim_1_out_5, dim_1_out_6, dim_1_out_7,
       dim_1_out_8, dim_1_out_9, dim_1_out_10, dim_1_out_11, dim_1_out_12, dim_1_out_13, dim_1_out_14,
       dim_1_out_15, dim_1_out_16, dim_1_out_17, jeu_1_out_1, jeu_1_out_2, jeu_1_out_3, jeu_1_out_4,
       jeu_1_out_5, jeu_1_out_6, jeu_1_out_7, jeu_1_out_8, jeu_1_out_9, jeu_1_out_10, jeu_1_out_11,
       jeu_1_out_12, jeu_1_out_13, jeu_1_out_14, jeu_1_out_15, jeu_1_out_16, jeu_1_out_17, lun_1_out_1,
       lun_1_out_2, lun_1_out_3, lun_1_out_4, lun_1_out_5, lun_1_out_6, lun_1_out_7, lun_1_out_8,
       lun_1_out_9, lun_1_out_10, lun_1_out_11, lun_1_out_12, lun_1_out_13, lun_1_out_14, lun_1_out_15,
       lun_1_out_16, lun_1_out_17, mard_1_out_1, mard_1_out_2, mard_1_out_3, mard_1_out_4, mard_1_out_5,
       mard_1_out_6, mard_1_out_7, mard_1_out_8, mard_1_out_9, mard_1_out_10, mard_1_out_11, mard_1_out_12,
       mard_1_out_13, mard_1_out_14, mard_1_out_15, mard_1_out_16, mard_1_out_17, mer_1_out_1, mer_1_out_2,
       mer_1_out_3, mer_1_out_4, mer_1_out_5, mer_1_out_6, mer_1_out_7, mer_1_out_8, mer_1_out_9,
       mer_1_out_10, mer_1_out_11, mer_1_out_12, mer_1_out_13, mer_1_out_14, mer_1_out_15, mer_1_out_16,
       mer_1_out_17, sam_1_out_1, sam_1_out_2, sam_1_out_3, sam_1_out_4, sam_1_out_5, sam_1_out_6,
       sam_1_out_7, sam_1_out_8, sam_1_out_9, sam_1_out_10, sam_1_out_11, sam_1_out_12, sam_1_out_13,
       sam_1_out_14, sam_1_out_15, sam_1_out_16, sam_1_out_17, ven_1_out_1, ven_1_out_2, ven_1_out_3,
       ven_1_out_4, ven_1_out_5, ven_1_out_6, ven_1_out_7, ven_1_out_8, ven_1_out_9, ven_1_out_10,
       ven_1_out_11, ven_1_out_12, ven_1_out_13, ven_1_out_14, ven_1_out_15, ven_1_out_16, ven_1_out_17;

  J_K_Flip_Flop j_k_ff_1 (
    .J(1'b1), .clk(CLOCK), .K(1'b1), .Q(j_k_ff_1_q[0]), .Qn(j_k_ff_1_qn), .reset(and_1_out));  // open: preset, en
  J_K_Flip_Flop j_k_ff_2 (
    .J(1'b1), .clk(j_k_ff_1_qn), .K(1'b1), .Q(j_k_ff_1_q[1]), .Qn(j_k_ff_2_qn), .reset(and_1_out));  // open: preset, en
  J_K_Flip_Flop j_k_ff_3 (
    .J(1'b1), .clk(j_k_ff_2_qn), .K(1'b1), .Q(j_k_ff_1_q[2]), .reset(and_1_out));  // open: Qn, preset, en
  Multiplexer #(.select(3), .width(6)) multiplexer_1 (
    .in0(lun_1_out_11), .in1(mard_1_out_11), .in2(mer_1_out_11), .in3(jeu_1_out_11), .in4(ven_1_out_11),
    .in5(sam_1_out_11), .in6(dim_1_out_11), .out(out_12), .sel(j_k_ff_1_q));  // open: in7, en
  Multiplexer #(.select(3), .width(6)) multiplexer_2 (
    .in0(lun_1_out_12), .in1(mard_1_out_12), .in2(mer_1_out_12), .in3(jeu_1_out_12), .in4(ven_1_out_12),
    .in5(sam_1_out_12), .in6(dim_1_out_12), .out(out_13), .sel(j_k_ff_1_q));  // open: in7, en
  Multiplexer #(.select(3), .width(6)) multiplexer_3 (
    .in0(lun_1_out_13), .in1(mard_1_out_13), .in2(mer_1_out_13), .in3(jeu_1_out_13), .in4(ven_1_out_13),
    .in5(sam_1_out_13), .in6(dim_1_out_13), .out(out_14), .sel(j_k_ff_1_q));  // open: in7, en
  Multiplexer #(.select(3), .width(6)) multiplexer_4 (
    .in0(lun_1_out_14), .in1(mard_1_out_14), .in2(mer_1_out_14), .in3(jeu_1_out_14), .in4(ven_1_out_14),
    .in5(sam_1_out_14), .in6(dim_1_out_14), .out(out_15), .sel(j_k_ff_1_q));  // open: in7, en
  Multiplexer #(.select(3), .width(6)) multiplexer_5 (
    .in0(lun_1_out_15), .in1(mard_1_out_15), .in2(mer_1_out_15), .in3(jeu_1_out_15), .in4(ven_1_out_15),
    .in5(sam_1_out_15), .in6(dim_1_out_15), .out(out_16), .sel(j_k_ff_1_q));  // open: in7, en
  Multiplexer #(.select(3), .width(6)) multiplexer_6 (
    .in0(lun_1_out_16), .in1(mard_1_out_16), .in2(mer_1_out_16), .in3(jeu_1_out_16), .in4(ven_1_out_16),
    .in5(sam_1_out_16), .in6(dim_1_out_16), .out(out_17), .sel(j_k_ff_1_q));  // open: in7, en
  Multiplexer #(.select(3), .width(6)) multiplexer_7 (
    .in0(lun_1_out_17), .in1(mard_1_out_17), .in2(mer_1_out_17), .in3(jeu_1_out_17), .in4(ven_1_out_17),
    .in5(sam_1_out_17), .in6(dim_1_out_17), .out(out_18), .sel(j_k_ff_1_q));  // open: in7, en
  and and_1 (and_1_out, j_k_ff_1_q[0], j_k_ff_1_q[1], j_k_ff_1_q[2]);
  Multiplexer #(.select(3), .width(6)) multiplexer_8 (
    .in0(lun_1_out_3), .in1(mard_1_out_3), .in2(mer_1_out_3), .in3(jeu_1_out_3), .in4(ven_1_out_3),
    .in5(sam_1_out_3), .in6(dim_1_out_3), .out(out_4), .sel(j_k_ff_1_q));  // open: in7, en
  Multiplexer #(.select(3), .width(6)) multiplexer_9 (
    .in0(lun_1_out_4), .in1(mard_1_out_4), .in2(mer_1_out_4), .in3(jeu_1_out_4), .in4(ven_1_out_4),
    .in5(sam_1_out_4), .in6(dim_1_out_4), .out(out_5), .sel(j_k_ff_1_q));  // open: in7, en
  Multiplexer #(.select(3), .width(6)) multiplexer_10 (
    .in0(lun_1_out_5), .in1(mard_1_out_5), .in2(mer_1_out_5), .in3(jeu_1_out_5), .in4(ven_1_out_5),
    .in5(sam_1_out_5), .in6(dim_1_out_5), .out(out_6), .sel(j_k_ff_1_q));  // open: in7, en
  lun lun_1 (
    .out_1(lun_1_out_1), .out_2(lun_1_out_2), .out_3(lun_1_out_3), .out_4(lun_1_out_4), .out_5(lun_1_out_5),
    .out_6(lun_1_out_6), .out_7(lun_1_out_7), .out_8(lun_1_out_8), .out_9(lun_1_out_9),
    .out_10(lun_1_out_10), .out_11(lun_1_out_11), .out_12(lun_1_out_12), .out_13(lun_1_out_13),
    .out_14(lun_1_out_14), .out_15(lun_1_out_15), .out_16(lun_1_out_16), .out_17(lun_1_out_17));
  Multiplexer #(.select(3), .width(6)) multiplexer_11 (
    .in0(lun_1_out_6), .in1(mard_1_out_6), .in2(mer_1_out_6), .in3(jeu_1_out_6), .in4(ven_1_out_6),
    .in5(sam_1_out_6), .in6(dim_1_out_6), .out(out_7), .sel(j_k_ff_1_q));  // open: in7, en
  Multiplexer #(.select(3), .width(6)) multiplexer_12 (
    .in0(lun_1_out_7), .in1(mard_1_out_7), .in2(mer_1_out_7), .in3(jeu_1_out_7), .in4(ven_1_out_7),
    .in5(sam_1_out_7), .in6(dim_1_out_7), .out(out_8), .sel(j_k_ff_1_q));  // open: in7, en
  Multiplexer #(.select(3), .width(6)) multiplexer_13 (
    .in0(lun_1_out_8), .in1(mard_1_out_8), .in2(mer_1_out_8), .in3(jeu_1_out_8), .in4(ven_1_out_8),
    .in5(sam_1_out_8), .in6(dim_1_out_8), .out(out_9), .sel(j_k_ff_1_q));  // open: in7, en
  Multiplexer #(.select(3), .width(6)) multiplexer_14 (
    .in0(lun_1_out_9), .in1(mard_1_out_9), .in2(mer_1_out_9), .in3(jeu_1_out_9), .in4(ven_1_out_9),
    .in5(sam_1_out_9), .in6(dim_1_out_9), .out(out_10), .sel(j_k_ff_1_q));  // open: in7, en
  Multiplexer #(.select(3), .width(6)) multiplexer_15 (
    .in0(lun_1_out_10), .in1(mard_1_out_10), .in2(mer_1_out_10), .in3(jeu_1_out_10), .in4(ven_1_out_10),
    .in5(sam_1_out_10), .in6(dim_1_out_10), .out(out_11), .sel(j_k_ff_1_q));  // open: in7, en
  Multiplexer #(.select(3), .width(6)) multiplexer_16 (
    .in0(lun_1_out_1), .in1(mard_1_out_1), .in2(mer_1_out_1), .in3(jeu_1_out_1), .in4(ven_1_out_1),
    .in5(sam_1_out_1), .in6(dim_1_out_1), .out(out_2), .sel(j_k_ff_1_q));  // open: in7, en
  Multiplexer #(.select(3), .width(6)) multiplexer_17 (
    .in0(lun_1_out_2), .in1(mard_1_out_2), .in2(mer_1_out_2), .in3(jeu_1_out_2), .in4(ven_1_out_2),
    .in5(sam_1_out_2), .in6(dim_1_out_2), .out(out_3), .sel(j_k_ff_1_q));  // open: in7, en
  mard mard_1 (
    .out_1(mard_1_out_1), .out_2(mard_1_out_2), .out_3(mard_1_out_3), .out_4(mard_1_out_4),
    .out_5(mard_1_out_5), .out_6(mard_1_out_6), .out_7(mard_1_out_7), .out_8(mard_1_out_8),
    .out_9(mard_1_out_9), .out_10(mard_1_out_10), .out_11(mard_1_out_11), .out_12(mard_1_out_12),
    .out_13(mard_1_out_13), .out_14(mard_1_out_14), .out_15(mard_1_out_15), .out_16(mard_1_out_16),
    .out_17(mard_1_out_17));
  mer mer_1 (
    .out_1(mer_1_out_1), .out_2(mer_1_out_2), .out_3(mer_1_out_3), .out_4(mer_1_out_4), .out_5(mer_1_out_5),
    .out_6(mer_1_out_6), .out_7(mer_1_out_7), .out_8(mer_1_out_8), .out_9(mer_1_out_9),
    .out_10(mer_1_out_10), .out_11(mer_1_out_11), .out_12(mer_1_out_12), .out_13(mer_1_out_13),
    .out_14(mer_1_out_14), .out_15(mer_1_out_15), .out_16(mer_1_out_16), .out_17(mer_1_out_17));
  jeu jeu_1 (
    .out_1(jeu_1_out_1), .out_2(jeu_1_out_2), .out_3(jeu_1_out_3), .out_4(jeu_1_out_4), .out_5(jeu_1_out_5),
    .out_6(jeu_1_out_6), .out_7(jeu_1_out_7), .out_8(jeu_1_out_8), .out_9(jeu_1_out_9),
    .out_10(jeu_1_out_10), .out_11(jeu_1_out_11), .out_12(jeu_1_out_12), .out_13(jeu_1_out_13),
    .out_14(jeu_1_out_14), .out_15(jeu_1_out_15), .out_16(jeu_1_out_16), .out_17(jeu_1_out_17));
  ven ven_1 (
    .out_1(ven_1_out_1), .out_2(ven_1_out_2), .out_3(ven_1_out_3), .out_4(ven_1_out_4), .out_5(ven_1_out_5),
    .out_6(ven_1_out_6), .out_7(ven_1_out_7), .out_8(ven_1_out_8), .out_9(ven_1_out_9),
    .out_10(ven_1_out_10), .out_11(ven_1_out_11), .out_12(ven_1_out_12), .out_13(ven_1_out_13),
    .out_14(ven_1_out_14), .out_15(ven_1_out_15), .out_16(ven_1_out_16), .out_17(ven_1_out_17));
  sam sam_1 (
    .out_1(sam_1_out_1), .out_2(sam_1_out_2), .out_3(sam_1_out_3), .out_4(sam_1_out_4), .out_5(sam_1_out_5),
    .out_6(sam_1_out_6), .out_7(sam_1_out_7), .out_8(sam_1_out_8), .out_9(sam_1_out_9),
    .out_10(sam_1_out_10), .out_11(sam_1_out_11), .out_12(sam_1_out_12), .out_13(sam_1_out_13),
    .out_14(sam_1_out_14), .out_15(sam_1_out_15), .out_16(sam_1_out_16), .out_17(sam_1_out_17));
  dim dim_1 (
    .out_1(dim_1_out_1), .out_2(dim_1_out_2), .out_3(dim_1_out_3), .out_4(dim_1_out_4), .out_5(dim_1_out_5),
    .out_6(dim_1_out_6), .out_7(dim_1_out_7), .out_8(dim_1_out_8), .out_9(dim_1_out_9),
    .out_10(dim_1_out_10), .out_11(dim_1_out_11), .out_12(dim_1_out_12), .out_13(dim_1_out_13),
    .out_14(dim_1_out_14), .out_15(dim_1_out_15), .out_16(dim_1_out_16), .out_17(dim_1_out_17));
endmodule

module finaaaaal (
  input  reset,
  input  clock,
  output [3:0] out_3,
  output [3:0] out_4,
  output [3:0] ms1,
  output [3:0] ms0,
  output [3:0] out_7,
  output [3:0] out_8,
  output [3:0] out_9,
  output [3:0] out_10,
  output [3:0] out_11,
  output [3:0] out_12,
  output [3:0] out_13,
  output [3:0] out_14,
  output [1:0] J1,
  output [3:0] J0,
  output [1:0] H1,
  output [3:0] H0,
  output [2:0] min1,
  output [3:0] min0,
  output M1,
  output [3:0] M0,
  output point,
  output xx
);

  wire ctp_secd_1_resert, ctp_secd_2_resert, houres_1_resert, jours_1_resert, ms_1_resert;

  mois mois_1 (
    .CLOCK(jours_1_resert), .mois1(out_7), .mois0(out_8), ._1(M1), ._0(M0), .resetforce(reset));  // open: resert
  jours jours_1 (
    .clock(houres_1_resert), .jrs1(out_9), .jrs0(out_10), .resert(jours_1_resert), ._1(J1), ._0(J0),
    .resetforc(reset), .xx(xx));
  HOURES houres_1 (
    .clock(ctp_secd_1_resert), .hrs1(out_11), .resert(houres_1_resert), .hrs0(out_12), ._1(H1), ._0(H0),
    .arretforc(reset));
  CTP_SECD ctp_secd_1 (
    .CLOCK(ctp_secd_2_resert), .SCD1(out_13), .resert(ctp_secd_1_resert), .SCD0(out_14), .sc1(min1),
    .sc0(min0), .restforc(reset));  // open: points
  CTP_SECD ctp_secd_2 (
    .CLOCK(ms_1_resert), .SCD1(out_3), .resert(ctp_secd_2_resert), .SCD0(out_4), .points(point),
    .restforc(reset));  // open: sc1, sc0
  ms ms_1 (.CLOCK(clock), .ms1(ms1), .ms0(ms0), .resert(ms_1_resert), .\resetforcé (reset));
endmodule

module FIN (
);

  wire clock, p, reset, xx;
  wire [3:0] h0, h1, J0, J1, m0, m1, min0, min1, ms0, ms1, s0, s1;
  wire [5:0] deco_jrs_1_out_2, deco_jrs_1_out_3, deco_jrs_1_out_4, deco_jrs_1_out_5, deco_jrs_1_out_6,
       deco_jrs_1_out_7, deco_jrs_1_out_8, deco_jrs_1_out_9, deco_jrs_1_out_10, deco_jrs_1_out_11,
       deco_jrs_1_out_12, deco_jrs_1_out_13, deco_jrs_1_out_14, deco_jrs_1_out_15, deco_jrs_1_out_16,
       deco_jrs_1_out_17, deco_jrs_1_out_18;

  Hex_Digit_Display hex_digit_display_1 (.value(m1));  // open: dp
  DotMatrix #(.matrixcols(17), .matrixrows(6)) dotmatrix_1 (
    .col0(deco_jrs_1_out_2), .col1(deco_jrs_1_out_3), .col2(deco_jrs_1_out_4), .col3(deco_jrs_1_out_5),
    .col4(deco_jrs_1_out_6), .col5(deco_jrs_1_out_7), .col6(deco_jrs_1_out_8), .col7(deco_jrs_1_out_9),
    .col8(deco_jrs_1_out_10), .col9(deco_jrs_1_out_11), .col10(deco_jrs_1_out_12), .col11(deco_jrs_1_out_13),
    .col12(deco_jrs_1_out_14), .col13(deco_jrs_1_out_15), .col14(deco_jrs_1_out_16),
    .col15(deco_jrs_1_out_17), .col16(deco_jrs_1_out_18));
  deco_jrs deco_jrs_1 (
    .CLOCK(xx), .out_2(deco_jrs_1_out_2), .out_3(deco_jrs_1_out_3), .out_4(deco_jrs_1_out_4),
    .out_5(deco_jrs_1_out_5), .out_6(deco_jrs_1_out_6), .out_7(deco_jrs_1_out_7), .out_8(deco_jrs_1_out_8),
    .out_9(deco_jrs_1_out_9), .out_10(deco_jrs_1_out_10), .out_11(deco_jrs_1_out_11),
    .out_12(deco_jrs_1_out_12), .out_13(deco_jrs_1_out_13), .out_14(deco_jrs_1_out_14),
    .out_15(deco_jrs_1_out_15), .out_16(deco_jrs_1_out_16), .out_17(deco_jrs_1_out_17),
    .out_18(deco_jrs_1_out_18));
  LED led_1 (.in(p));
  LED led_2 (.in(p));
  Hex_Digit_Display hex_digit_display_2 (.value(m0));  // open: dp
  Hex_Digit_Display hex_digit_display_3 (.value(J1));  // open: dp
  Hex_Digit_Display hex_digit_display_4 (.value(J0));  // open: dp
  LED led_3 (.in(p));
  LED led_4 (.in(p));
  finaaaaal finaaaaal_1 (
    .out_7(m1), .out_8(m0), .out_9(J1), .out_10(J0), .out_11(h1), .out_12(h0), .out_13(min1), .out_14(min0),
    .out_3(s1), .out_4(s0), .ms1(ms1), .ms0(ms0), .reset(reset), .point(p), .clock(clock), .xx(xx));  // open: M1, M0, J1, J0, H1, H0, min1, min0
  Hex_Digit_Display hex_digit_display_5 (.value(h0));  // open: dp
  Hex_Digit_Display hex_digit_display_6 (.value(h1));  // open: dp
  LED led_5 (.in(p));
  LED led_6 (.in(p));
  Hex_Digit_Display hex_digit_display_7 (.value(min1));  // open: dp
  LED led_7 (.in(p));
  LED led_8 (.in(p));
  Hex_Digit_Display hex_digit_display_8 (.value(min0));  // open: dp
  Hex_Digit_Display hex_digit_display_9 (.value(s0));  // open: dp
  Hex_Digit_Display hex_digit_display_10 (.value(s1));  // open: dp
  LED led_9 (.in(p));
  LED led_10 (.in(p));
  Hex_Digit_Display hex_digit_display_11 (.value(ms1));  // open: dp
  Hex_Digit_Display hex_digit_display_12 (.value(ms0));  // open: dp
  Clock clock_1 (.out(clock));
  Button restfirc (.out(reset));

  // Notes on the sheet:
  //   MOIS
  //   JRS
  //   HRS
  //   MIN
  //   S
  //   MS
endmodule
